# Fritzing sketch dotstar (saved by Fritzing 0.9.3b)
breadboards: 1

parts:
  Pew1 = PewPew 10
  DOTSTAR1 = DotStar Strip -- Black (60/m) [part_number=2239]

nets:
  N1: Pew1.+3V_2, DOTSTAR1.+5V
  N2: Pew1.P2, DOTSTAR1.CI
  N3: Pew1.P1, DOTSTAR1.DI
  N4: Pew1.-GND_1, DOTSTAR1.GND

custom parts:
  PewPew 10: Pewpew 10 with 12-pin connector, schematic
  DotStar Strip -- Black (60/m): NeopixelDotStar Strip, Black, 60 pixels per meter.
