# Fritzing sketch ldr (saved by Fritzing 0.9.3b)
breadboards: 1

parts:
  Pew1 = PewPew 10
  R1 = Photocell (LDR) [package=THT]
  R2 = Resistor [tolerance=±5% resistance=10k package=THT]

nets:
  N1: Pew1.+3V_2, R1.pin_0
  N2: Pew1.P5, R1.pin_1, R2.Pin_0
  N3: Pew1.-GND_2, R2.Pin_1

custom parts:
  PewPew 10: Pewpew 10 with 12-pin connector, schematic
