# Fritzing sketch led (saved by Fritzing 0.9.3b)
breadboards: 2

parts:
  Pew1 = PewPew 10
  R3 = Resistor [tolerance=±5% resistance=220 package=THT]
  LED3 = LED - 5mm [color="Red (633nm)" package="5 mm [THT]"]
  Pew2 = PewPew 10
  LED4 = RGB LED (com. cathode, rgb) [package="5 mm [THT]"]
  LED5 = RGB LED (com. cathode, rgb) [package="5 mm [THT]"]  # not connected
  R4 = Resistor [tolerance=±5% resistance=1k package=THT]
  R5 = Resistor [tolerance=±5% resistance=220 package=THT]
  R6 = Resistor [tolerance=±5% resistance=220 package=THT]
  LED6 = LED - 5mm [color="Red (633nm)" package="5 mm [THT]"]  # not connected

nets:
  N1: Pew1.P1, R3.Pin_0
  N2: Pew1.-GND_2, LED3.cathode
  N3: R3.Pin_1, LED3.anode
  N4: Pew2.P4, R6.Pin_0
  N5: Pew2.P3, R4.Pin_0
  N6: Pew2.P1, R5.Pin_0
  N7: Pew2.-GND_2, LED4.green_anode
  N8: LED4.red_anode, R6.Pin_1
  N9: LED4.common_cathode, R4.Pin_1
  N10: LED4.blue_anode, R5.Pin_1

custom parts:
  PewPew 10: Pewpew 10 with 12-pin connector, schematic
