# Fritzing sketch potentiometer (saved by Fritzing 0.9.3b)
breadboards: 1

parts:
  POT1 = Breadboard Trimpot
  Pew1 = PewPew 10

nets:
  N1: POT1.PIN1, Pew1.-GND_2
  N2: POT1.PIN2, Pew1.P5
  N3: POT1.PIN3, Pew1.+3V_1

custom parts:
  PewPew 10: Pewpew 10 with 12-pin connector, schematic
