# Fritzing sketch pewpew-10.2 (saved by Fritzing 0.9.3b)
circuit board: 7.00001cm x 3.19999cm
breadboards: 1

parts:
  0N_0FF = SPST Switch [package=switch-spst-smd-a]
  U1 = prefix0000 [chip_label=SAMD21]
  X1a = mystery part, 8 pins [chip_label="LED Matrix"]
  X1b = mystery part, 8 pins [chip_label="LED Matrix"]
  o = SWITCH-MOMENTARY-2 [package=tactile_switch_tall]
  → = SWITCH-MOMENTARY-2 [package=tactile_switch_tall]
  ↓ = SWITCH-MOMENTARY-2 [package=tactile_switch_tall]
  ← = SWITCH-MOMENTARY-2 [package=tactile_switch_tall]
  x = SWITCH-MOMENTARY-2 [package=tactile_switch_tall]
  ↑ = SWITCH-MOMENTARY-2 [package=tactile_switch_tall]
  X2 = USB Connectors [package=usb-microb]
  - = female pin header, 1 pin [form="♀ (female)"]
  + = female pin header, 1 pin [form="♀ (female)"]
  +_2 = female pin header, 1 pin [form="♀ (female)"]
  -_2 = female pin header, 1 pin [form="♀ (female)"]
  U2 = Voltage Regulator [package=sot23-5]
  C1 = Ceramic Capacitor [capacitance=1µF package="0603 [SMD, multilayer]"]
  C2 = Ceramic Capacitor [capacitance=1µF package="0603 [SMD, multilayer]"]
  Pad1 = Pad [width=2.6000000000000001 height=2.6000000000000001 connect=center]
  J1 = female alternating pin header, 12 pins [form="♀ (female)"]

nets:
  N1: 0N_0FF.O, U2.OUT
  3.3V: 0N_0FF.P, U1.connector8, U1.connector29, C1.0, J1.pin11, J1.pin12
  N2: 0N_0FF.S, +.pin1, +_2.pin1
  N3: U1.connector0, J1.pin6
  N4: U1.connector1, J1.pin7
  N5: U1.connector2, J1.pin8
  N6: U1.connector3, J1.pin9
  N7: U1.connector4, J1.pin10
  R1: U1.connector5, X1b.pin8
  C4: U1.connector6, X1b.pin7
  C6: U1.connector7, X1b.pin6, ↑.2
  GND: U1.connector9, U1.connector27, X2.GND, -.pin1, -_2.pin1, U2.GND, C1.1, C2.1, Pad1.pad, J1.pin2, J1.pin3
  BUTTONS: U1.connector10, o.2, →.2, ↓.2, ←.2, x.1, ↑.1
  R4: U1.connector11, X1b.pin5
  C1: U1.connector12, X1b.pin4, →.1
  R2: U1.connector13, X1b.pin3
  C7: U1.connector14, X1b.pin2, ←.1
  C8: U1.connector15, X1b.pin1, ↓.1
  R5: U1.connector16, X1a.pin1
  R7: U1.connector17, X1a.pin2
  C2: U1.connector18, X1a.pin3, x.2
  C3: U1.connector19, X1a.pin4, o.1
  R8: U1.connector20, X1a.pin5
  C5: U1.connector21, X1a.pin6
  N8: U1.connector22, X2.D-
  N9: U1.connector23, X2.D+
  R6: U1.connector24, X1a.pin7
  RST: U1.connector25, J1.pin1
  R3: U1.connector26, X1a.pin8
  N10: U1.connector28, C2.0
  SWC: U1.connector30, J1.pin4
  SWD: U1.connector31, J1.pin5
  N11: X2.VBUS, U2.IN, U2.EN

notes:
  1
  R - - 1 2 3 4 5 6 7 + +3V
  PewPew v10.2
  Pew
  v10.2
  http://pewpew.rtfd.io
