# Fritzing sketch pewpewlite-4.0b (saved by Fritzing 0.9.3b)
circuit board: 5.05996cm x 2.26603cm
breadboards: 1

parts:
  S8 = SWITCH-MOMENTARY-2 [package=tactile_switch_tall]
  PewPew = SWITCH-MOMENTARY-2 [package=tactile_switch_tall]
  v2_0 = SWITCH-MOMENTARY-2 [package=tactile_switch_tall]
  o = SWITCH-MOMENTARY-2 [package=tactile_switch_tall]
  J2 = female pin header, 16 pins [form="♀ (female)"]
  Adafruit_Feather = female pin header, 12 pins [form="♀ (female)"]
  Lite = SWITCH-MOMENTARY-2 [package=tactile_switch_tall]
  x = SWITCH-MOMENTARY-2 [package=tactile_switch_tall]
  HT16K33 = SO-28x [chip_label=IC package=SO(x)]
  R2 = Resistor [tolerance=±5% resistance=4.7k package="0805 [SMD]"]
  R1 = Resistor [tolerance=±5% resistance=4.7k package="0805 [SMD]"]
  R3 = Resistor [tolerance=±5% resistance=10k package="0805 [SMD]"]
  R4 = Resistor [tolerance=±5% resistance=10k package="0805 [SMD]"]
  R5 = Resistor [tolerance=±5% resistance=10k package="0805 [SMD]"]
  R6 = Resistor [tolerance=±5% resistance=10k package="0805 [SMD]"]
  R7 = Resistor [tolerance=±5% resistance=39k package="0805 [SMD]"]
  R8 = Resistor [tolerance=±5% resistance=10k package="0805 [SMD]"]
  power = SWITCH_SPDT [package=kps-1290]
  +_- = mystery part, 2 pins [chip_label=battery]
  J5 = female pin header, 8 pins [form="♀ (female)"]
  J7 = female pin header, 8 pins [form="♀ (female)"]
  J6 = female pin header, 8 pins [form="♀ (female)"]

nets:
  COM1: S8.2, PewPew.2, v2_0.2, o.2, Lite.1, x.1, HT16K33.3, J7.pin7
  N1: S8.1, R8.Pin_1
  N2: PewPew.1, R4.Pin_1
  N3: v2_0.1, R5.Pin_1
  N4: o.1, R3.Pin_1
  3.3V: J2.pin2, HT16K33.28, R2.Pin_1, R1.Pin_1
  GND: J2.pin4, HT16K33.1, +_-.pin1
  N5: Adafruit_Feather.pin1, power.O
  N6: Adafruit_Feather.pin11, HT16K33.26, R1.Pin_0
  N7: Adafruit_Feather.pin12, HT16K33.27, R2.Pin_0
  N8: Lite.2, R6.Pin_1
  N9: x.2, R7.Pin_1
  COM0: HT16K33.2, J7.pin8
  COM2: HT16K33.4, J7.pin6
  COM3: HT16K33.5, J7.pin5
  COM4: HT16K33.6, J7.pin4
  COM5: HT16K33.7, J7.pin3
  COM6: HT16K33.8, J7.pin2
  COM7: HT16K33.9, J7.pin1
  ROW15: HT16K33.10, J5.pin1
  ROW14: HT16K33.11, J5.pin2
  ROW13: HT16K33.12, R3.Pin_0, J5.pin3
  ROW12: HT16K33.13, R4.Pin_0, J5.pin4
  ROW11: HT16K33.14, R5.Pin_0, J5.pin5
  ROW10: HT16K33.15, R6.Pin_0, J5.pin6
  ROW9: HT16K33.16, R8.Pin_0, J5.pin7
  ROW8: HT16K33.17, R7.Pin_0, J5.pin8
  ROW7: HT16K33.18, J6.pin1
  ROW6: HT16K33.19, J6.pin2
  ROW5: HT16K33.20, J6.pin3
  ROW4: HT16K33.21, J6.pin4
  ROW3: HT16K33.22, J6.pin5
  ROW2: HT16K33.23, J6.pin6
  ROW1: HT16K33.24, J6.pin7
  ROW0: HT16K33.25, J6.pin8
  N10: power.P, power.S, +_-.pin2

notes:
  PewPew Lite v4.0
  http://hackaday.io/
  /project/21578
  PewPew Lite 4.0, A game FeatherWing for the Adafruit Feather boards., 4.0
